// Logisim project cpu.circ as structural Verilog: 4 circuits, main circuit cpu
module cpu (
);

  wire clock_1_out, RST;
  wire [15:0] \总周期数 , \无条件分支指令数 , \有条件分支成功跳转 , \有条件分支指令数 ;
  wire [23:0] divider_1_out_2;
  wire [31:0] npc_1_out_2, PC_q, rom_1_data, SyscallOut;

  Button \u_总复位  (.out(RST));
  NPC npc_1 (.in_1(PC_q), .out_2(npc_1_out_2));
  Register #(.width(32)) PC (.D(npc_1_out_2), .Q(PC_q), .clk(clock_1_out));  // open: en, clr
  Clock clock_1 (.out(clock_1_out));
  Hex_Digit_Display hex_digit_display_1 (.value(SyscallOut[27:24]));  // open: dp
  Hex_Digit_Display hex_digit_display_2 (.value(SyscallOut[31:28]));  // open: dp
  Divider divider_1 (.in_1(PC_q), .out_2(divider_1_out_2));
  Hex_Digit_Display hex_digit_display_3 (.value(SyscallOut[23:20]));  // open: dp
  Hex_Digit_Display hex_digit_display_4 (.value(SyscallOut[19:16]));  // open: dp
  Hex_Digit_Display hex_digit_display_5 (.value(SyscallOut[11:8]));  // open: dp
  Hex_Digit_Display hex_digit_display_6 (.value(SyscallOut[15:12]));  // open: dp
  Controller controller_1 (.in_1(rom_1_data));
  ROM #(.addrWidth(24), .dataWidth(32)) rom_1 (.addr(divider_1_out_2), .data(rom_1_data));  // open: sel
  Hex_Digit_Display hex_digit_display_7 (.value(SyscallOut[7:4]));  // open: dp
  Hex_Digit_Display hex_digit_display_8 (.value(SyscallOut[3:0]));  // open: dp
  // Probe on \总周期数 
  // Probe on \无条件分支指令数 
  // Probe on \有条件分支指令数 
  // Probe on \有条件分支成功跳转 
  // RegisterFile registerfile_1: pin names not known; wires that end beside it: clock_1_out
  // ALU alu_1: pin names not known
  // MIPS_RAM mips_ram_1: pin names not known

  // Notes on the sheet:
  //   数码管输出应该用寄存器锁存，否则显示数据只能一闪而过
  //   可以通过项目增加Logisim库的方式将前几次实验完成的电路作为子电路引入到本电路中使用
  //   数码管输出
  //   总复位信号应将除ROM以外所有存储组件全部清零
endmodule

module Controller (
  input  [31:0] in_1
);


  // Other names for the same wires on the sheet: Instruction[31:0] = in_1
endmodule

module Divider (
  input  [31:0] in_1,
  output [23:0] out_2
);


  assign out_2 = in_1[25:2];

  // Other names for the same wires on the sheet: Input[31:0] = in_1; Output[23:0] = in_1[25:2]
endmodule

module NPC (
  input  [31:0] in_1,
  output [31:0] out_2
);

  Adder #(.width(32)) adder_1 (.a(in_1), .b(32'h4), .out(out_2));  // open: cin, cout

  // Other names for the same wires on the sheet: Input[31:0] = in_1; Output[31:0] = out_2
endmodule
